// Digital circuit BranchControl.dig as structural Verilog
module BranchControl (
  input  [6:0] OpCode,
  input  [2:0] Funct3,
  input  Zero,
  output Y
);

  wire and_1_out, and_2_out, and_3_out, and_4_out, not_1_out, not_2_out, not_3_out, not_4_out, not_5_out,
       not_6_out, not_7_out;

  not not_1 (not_1_out, OpCode[4]);
  not not_2 (not_2_out, OpCode[3]);
  not not_3 (not_3_out, OpCode[2]);
  not not_4 (not_4_out, Funct3[2]);
  not not_5 (not_5_out, Funct3[1]);
  not not_6 (not_6_out, Funct3[0]);
  not not_7 (not_7_out, Zero);
  and and_1 (and_1_out, OpCode[6], OpCode[5], not_1_out, not_2_out, not_3_out, OpCode[1], OpCode[0], not_4_out, not_5_out, not_6_out, Zero);
  and and_2 (and_2_out, OpCode[6], OpCode[5], not_1_out, not_2_out, not_3_out, OpCode[1], OpCode[0], not_4_out, not_5_out, Funct3[0], not_7_out);
  and and_3 (and_3_out, OpCode[6], OpCode[5], not_1_out, not_2_out, not_3_out, OpCode[1], OpCode[0], Funct3[2], not_5_out, not_6_out, not_7_out);
  and and_4 (and_4_out, OpCode[6], OpCode[5], not_1_out, not_2_out, not_3_out, OpCode[1], OpCode[0], Funct3[2], not_5_out, Funct3[0], Zero);
  or or_1 (Y, and_1_out, and_2_out, and_3_out, and_4_out);
endmodule
