// Digital circuit ControlUnit.dig as structural Verilog
module ControlUnit (
  input  [6:0] OpCode,
  input  [2:0] Funct3,
  input  [6:0] Funct7,
  input  Zero,
  output RegWrite,
  output [1:0] ImmSrc,
  output MemWrite,
  output [1:0] ResultSrc,
  output ALUSrc,
  output [2:0] ALUControl,
  output [1:0] PCSrc,
  output MemRead
);

  wire [0:0] branchcontrol_1_y, maindecoderv2_1_branch;
  wire [1:0] and_1_out, maindecoderv2_1_aluop, maindecoderv2_1_pcupdate;

  BranchControl branchcontrol_1 (.OpCode(OpCode), .Funct3(Funct3), .Zero(Zero), .Y(branchcontrol_1_y[0]));
  mainDecoderV2 maindecoderv2_1 (
    .OpCode(OpCode), .RegWrite(RegWrite), .ImmSrc(ImmSrc), .MemWrite(MemWrite), .ResultSrc(ResultSrc),
    .Branch(maindecoderv2_1_branch[0]), .ALUOp(maindecoderv2_1_aluop), .PCUpdate(maindecoderv2_1_pcupdate),
    .ALUSrc(ALUSrc), .MemRead(MemRead));
  aluDecoder aludecoder_1 (
    .AluOp(maindecoderv2_1_aluop), .Funct3(Funct3), .Op_5(OpCode[5]), .Funct7_5(Funct7[5]),
    .ALUControl(ALUControl));
  assign and_1_out = {1'b0, branchcontrol_1_y[0]} & {1'b0, maindecoderv2_1_branch[0]};  // And and_1, 2 bits wide
  assign PCSrc = and_1_out | maindecoderv2_1_pcupdate;  // Or or_1, 2 bits wide
endmodule
