// Digital circuit ExM.dig as structural Verilog
module ExM (
  input  RwIn,
  input  MwIn,
  input  [1:0] ResIn,
  input  MrIn,
  input  [23:0] AresIn,
  input  [31:0] DbIn,
  input  [4:0] RdIn,
  input  [31:0] Pc_plus_4In,
  input  CLK,
  output RwOut,
  output MwOut,
  output [1:0] ResOut,
  output MrOut,
  output [23:0] AresOut,
  output [31:0] DbOut,
  output [4:0] RdOut,
  output [31:0] Pc_plus_4Out
);

  Register register_1 (.D(RwIn), .C(CLK), .en(1'b1), .Q(RwOut));
  Register register_2 (.D(MwIn), .C(CLK), .en(1'b1), .Q(MwOut));
  Register #(.Bits(2)) register_3 (.D(ResIn), .C(CLK), .en(1'b1), .Q(ResOut));
  Register register_4 (.D(MrIn), .C(CLK), .en(1'b1), .Q(MrOut));
  Register #(.Bits(24)) register_5 (.D(AresIn), .C(CLK), .en(1'b1), .Q(AresOut));
  Register #(.Bits(32)) register_6 (.D(DbIn), .C(CLK), .en(1'b1), .Q(DbOut));
  Register #(.Bits(5)) register_7 (.D(RdIn), .C(CLK), .en(1'b1), .Q(RdOut));
  Register #(.Bits(32)) register_8 (.D(Pc_plus_4In), .C(CLK), .en(1'b1), .Q(Pc_plus_4Out));
endmodule
