// Digital circuit HazardDetectionUnit.dig as structural Verilog
module HazardDetectionUnit (
  input  [4:0] Rd1,
  input  [4:0] Rd2,
  input  [4:0] Rs,
  input  [4:0] Rt,
  input  [4:0] Rd3,
  input  AluSrc,
  output [1:0] RsHazard,
  output [2:0] RtHazard
);

  wire and_1_out, and_2_out, and_3_out, and_5_out, and_6_out, and_7_out, comparator_1_eq, comparator_2_eq,
       comparator_3_eq, comparator_4_eq, comparator_5_eq, comparator_6_eq, not_1_out, not_2_out, not_3_out,
       not_4_out, not_5_out;

  Comparator #(.Bits(5)) comparator_1 (.a(Rs), .b(Rd1), .eq(comparator_1_eq));  // open: gt, lt
  Comparator #(.Bits(5)) comparator_2 (.a(Rt), .b(Rd1), .eq(comparator_2_eq));  // open: gt, lt
  Comparator #(.Bits(5)) comparator_3 (.a(Rs), .b(Rd2), .eq(comparator_3_eq));  // open: gt, lt
  Comparator #(.Bits(5)) comparator_4 (.a(Rt), .b(Rd2), .eq(comparator_4_eq));  // open: gt, lt
  Comparator #(.Bits(5)) comparator_5 (.a(Rs), .b(Rd3), .eq(comparator_5_eq));  // open: gt, lt
  Comparator #(.Bits(5)) comparator_6 (.a(Rt), .b(Rd3), .eq(comparator_6_eq));  // open: gt, lt
  not not_1 (not_1_out, comparator_1_eq);
  not not_2 (not_2_out, comparator_2_eq);
  not not_3 (not_3_out, comparator_3_eq);
  not not_4 (not_4_out, comparator_4_eq);
  and and_1 (and_1_out, not_1_out, comparator_5_eq);
  and and_2 (and_2_out, not_1_out, comparator_3_eq);
  and and_3 (and_3_out, not_3_out, comparator_5_eq);
  not not_5 (not_5_out, AluSrc);
  and and_4 (RtHazard[2], not_5_out, not_2_out, not_4_out, comparator_6_eq);
  and and_5 (and_5_out, not_5_out, comparator_4_eq);
  and and_6 (and_6_out, not_5_out, comparator_2_eq);
  and and_7 (and_7_out, not_2_out, comparator_4_eq);
  or or_1 (RsHazard[1], and_1_out, and_2_out);
  or or_2 (RsHazard[0], comparator_1_eq, and_3_out);
  or or_3 (RtHazard[1], and_5_out, and_6_out);
  or or_4 (RtHazard[0], AluSrc, and_7_out);
endmodule
