// Digital circuit IDEX.dig as structural Verilog
module IDEX (
  input  RwIn,
  input  MwIn,
  input  [1:0] ResIn,
  input  [2:0] ActrlIn,
  input  [1:0] PcSrcIn,
  input  MrIn,
  input  [31:0] DaIn,
  input  [31:0] DbIn,
  input  [4:0] RdIn,
  input  [31:0] ImmIn,
  input  [31:0] PcIn,
  input  [31:0] Pc_plus_4In,
  input  CLK,
  input  [1:0] RsHazardIn,
  input  [2:0] RtHazardIn,
  output RwOut,
  output MwOut,
  output [1:0] ResOu,
  output [2:0] ActrlOut,
  output [1:0] PcSrcOut,
  output MrOut,
  output [31:0] DaOut,
  output [31:0] DbOut,
  output [4:0] RdOut,
  output [31:0] ImmOut,
  output [31:0] PcOut,
  output [31:0] Pc_plus_4Out,
  output [1:0] RsHazardOut,
  output [2:0] RtHazardOut
);

  Register #(.Bits(2)) register_1 (.D(RsHazardIn), .C(CLK), .en(1'b1), .Q(RsHazardOut));
  Register #(.Bits(3)) register_2 (.D(RtHazardIn), .C(CLK), .en(1'b1), .Q(RtHazardOut));
  Register register_3 (.D(RwIn), .C(CLK), .en(1'b1), .Q(RwOut));
  Register register_4 (.D(MwIn), .C(CLK), .en(1'b1), .Q(MwOut));
  Register #(.Bits(2)) register_5 (.D(ResIn), .C(CLK), .en(1'b1), .Q(ResOu));
  Register #(.Bits(3)) register_6 (.D(ActrlIn), .C(CLK), .en(1'b1), .Q(ActrlOut));
  Register #(.Bits(2)) register_7 (.D(PcSrcIn), .C(CLK), .en(1'b1), .Q(PcSrcOut));
  Register register_8 (.D(MrIn), .C(CLK), .en(1'b1), .Q(MrOut));
  Register #(.Bits(32)) register_9 (.D(DaIn), .C(CLK), .en(1'b1), .Q(DaOut));
  Register #(.Bits(32)) register_10 (.D(DbIn), .C(CLK), .en(1'b1), .Q(DbOut));
  Register #(.Bits(5)) register_11 (.D(RdIn), .C(CLK), .en(1'b1), .Q(RdOut));
  Register #(.Bits(32)) register_12 (.D(ImmIn), .C(CLK), .en(1'b1), .Q(ImmOut));
  Register #(.Bits(32)) register_13 (.D(PcIn), .C(CLK), .en(1'b1), .Q(PcOut));
  Register #(.Bits(32)) register_14 (.D(Pc_plus_4In), .C(CLK), .en(1'b1), .Q(Pc_plus_4Out));
endmodule
