// Digital circuit IFID.dig as structural Verilog
module IFID (
  input  [31:0] InsIn,
  input  [31:0] PcIn,
  input  [31:0] Pc_plus_4In,
  input  CLK,
  output [31:0] InsOut,
  output [31:0] PcOut,
  output [31:0] Pc_plus_4Out
);

  Register #(.Bits(32)) register_1 (.D(InsIn), .C(CLK), .en(1'b1), .Q(InsOut));
  Register #(.Bits(32)) register_2 (.D(PcIn), .C(CLK), .en(1'b1), .Q(PcOut));
  Register #(.Bits(32)) register_3 (.D(Pc_plus_4In), .C(CLK), .en(1'b1), .Q(Pc_plus_4Out));
  // Pins of 1 and 32 bits meet at InsOut
  // Pins of 1 and 32 bits meet at PcOut
  // Pins of 1 and 32 bits meet at Pc_plus_4Out
endmodule
