// Digital circuit MWB.dig as structural Verilog
module MWB (
  input  RwIn,
  input  [1:0] ResIn,
  input  [31:0] MemIn,
  input  [31:0] AresIn,
  input  [4:0] RdIn,
  input  [31:0] Pc_plus_4In,
  input  CLK,
  output RwOut,
  output [1:0] ResOut,
  output [31:0] MemOut,
  output [31:0] AresOut,
  output [4:0] RdOut,
  output [31:0] Pc_plus_4Out
);

  Register register_1 (.D(RwIn), .C(CLK), .en(1'b1), .Q(RwOut));
  Register #(.Bits(2)) register_2 (.D(ResIn), .C(CLK), .en(1'b1), .Q(ResOut));
  Register #(.Bits(32)) register_3 (.D(MemIn), .C(CLK), .en(1'b1), .Q(MemOut));
  Register #(.Bits(32)) register_4 (.D(AresIn), .C(CLK), .en(1'b1), .Q(AresOut));
  Register #(.Bits(5)) register_5 (.D(RdIn), .C(CLK), .en(1'b1), .Q(RdOut));
  Register #(.Bits(32)) register_6 (.D(Pc_plus_4In), .C(CLK), .en(1'b1), .Q(Pc_plus_4Out));
endmodule
