// Digital circuit Main.dig as structural Verilog
module Main (
  input  clk
);

  wire ALU_zero, EX_MEM_mrout, EX_MEM_mwout, EX_MEM_rwout, ID_EX_p16, ID_EX_p17, ID_EX_p21, IF_ID_p6,
       IF_ID_p7, MEM_WB_rwout, Unidade_de_Controle_alusrc, Unidade_de_Controle_memread,
       Unidade_de_Controle_memwrite, Unidade_de_Controle_regwrite;
  wire [1:0] EX_MEM_resout, hazarddetectionunit_1_rshazard, ID_EX_p18, ID_EX_p20, ID_EX_p28, MEM_WB_resout,
       Unidade_de_Controle_immsrc, Unidade_de_Controle_pcsrc, Unidade_de_Controle_resultsrc;
  wire [2:0] hazarddetectionunit_1_rthazard, ID_EX_p19, ID_EX_p29, IF_ID_p5_3, Unidade_de_Controle_alucontrol;
  wire [4:0] EX_MEM_rdout, ID_EX_p24, IF_ID_p5_2, IF_ID_p5_4, MEM_WB_rdout;
  wire [6:0] IF_ID_p5, IF_ID_p5_6;
  wire [17:13] IF_ID_p5_5;
  wire [23:0] ALU_s, EX_MEM_aresout, multiplexer_1_out, PC__plus__eq__4_s, PC_q;
  wire [31:0] Banco_de_Registradores_da, Banco_de_Registradores_db, bitextender_1_out, bitextender_2_out,
       bitextender_3_out, EX_MEM_dbout, EX_MEM_pc_plus_4out, Extensor_de_Sinal_ext, ID_EX_p22, ID_EX_p23,
       ID_EX_p25, ID_EX_p26, ID_EX_p27, MEM_WB_aresout, MEM_WB_memout, MEM_WB_pc_plus_4out,
       \Memória_de_Dados_d , \Memória_de_Instruções_d , multiplexer_2_out, multiplexer_3_out,
       multiplexer_4_out, PC__plus__IMM_s, RS1__plus__IMM_s, WbBackup_q;
  wire [31:24] ALU_s_2, multiplexer_1_out_2;

  Multiplexer #(.Selector_Bits(2), .Bits(32)) multiplexer_1 (
    .sel(ID_EX_p20), .in_0(bitextender_2_out), .in_1(PC__plus__IMM_s), .in_2(RS1__plus__IMM_s),
    .in_3({32{1'b0}}), .out({multiplexer_1_out_2, multiplexer_1_out}));
  Register #(.Bits(24)) PC (.D(multiplexer_1_out), .C(clk), .en(\Memória_de_Instruções_d [0]), .Q(PC_q));
  ROM #(.AddrBits(24), .Bits(32)) \Memória_de_Instruções  (.A(PC_q), .sel(1'b1), .D(\Memória_de_Instruções_d ));
  BitExtender #(.inputBits(24), .outputBits(32)) bitextender_1 (.in(PC_q), .out(bitextender_1_out));
  Add #(.Bits(24)) PC__plus__eq__4 (.a(PC_q), .b(24'h4), .c_i(1'b0), .s(PC__plus__eq__4_s));  // open: c_o
  BitExtender #(.inputBits(24), .outputBits(32)) bitextender_2 (.in(PC__plus__eq__4_s), .out(bitextender_2_out));
  // IFID IF_ID: pin names not known; wires that end beside it: \Memória_de_Instruções_d , bitextender_1_out, bitextender_2_out, clk, {IF_ID_p5_6, IF_ID_p5_5, IF_ID_p5_4, IF_ID_p5_3, IF_ID_p5_2, IF_ID_p5}, IF_ID_p6, IF_ID_p7
  HazardDetectionUnit hazarddetectionunit_1 (
    .Rd1(ID_EX_p24), .Rd2(EX_MEM_rdout), .Rs(IF_ID_p5_4), .Rt(IF_ID_p5_4), .Rd3(MEM_WB_rdout),
    .AluSrc(Unidade_de_Controle_alusrc), .RsHazard(hazarddetectionunit_1_rshazard),
    .RtHazard(hazarddetectionunit_1_rthazard));
  ControlUnit Unidade_de_Controle (
    .OpCode(IF_ID_p5), .Funct3(IF_ID_p5_3), .Funct7(IF_ID_p5_6), .Zero(ALU_zero),
    .RegWrite(Unidade_de_Controle_regwrite), .ImmSrc(Unidade_de_Controle_immsrc),
    .MemWrite(Unidade_de_Controle_memwrite), .ResultSrc(Unidade_de_Controle_resultsrc),
    .ALUSrc(Unidade_de_Controle_alusrc), .ALUControl(Unidade_de_Controle_alucontrol),
    .PCSrc(Unidade_de_Controle_pcsrc), .MemRead(Unidade_de_Controle_memread));
  RegisterFile #(.AddrBits(5), .Bits(32)) Banco_de_Registradores (
    .Din(multiplexer_4_out), .we(MEM_WB_rwout), .Rw(MEM_WB_rdout), .C(clk), .Ra(IF_ID_p5_4), .Rb(IF_ID_p5_5),
    .Da(Banco_de_Registradores_da), .Db(Banco_de_Registradores_db));
  SignExtender Extensor_de_Sinal (
    .ImmSrc(Unidade_de_Controle_immsrc),
    .OpCode_31_7({IF_ID_p5_6, IF_ID_p5_5, IF_ID_p5_4, IF_ID_p5_3, IF_ID_p5_2}), .EXT(Extensor_de_Sinal_ext));
  // IDEX ID_EX: pin names not known; wires that end beside it: Unidade_de_Controle_regwrite, Unidade_de_Controle_memwrite, Unidade_de_Controle_resultsrc, Unidade_de_Controle_alucontrol, Unidade_de_Controle_pcsrc, Unidade_de_Controle_memread, Banco_de_Registradores_da, Banco_de_Registradores_db, IF_ID_p5_2, Extensor_de_Sinal_ext, IF_ID_p6, IF_ID_p7, clk, hazarddetectionunit_1_rshazard, hazarddetectionunit_1_rthazard, ID_EX_p16, ID_EX_p17, ID_EX_p18, ID_EX_p19, ID_EX_p20, ID_EX_p21, ID_EX_p22, ID_EX_p23, ID_EX_p24, ID_EX_p25, ID_EX_p26, ID_EX_p27, ID_EX_p28, ID_EX_p29
  Add #(.Bits(32)) RS1__plus__IMM (.a(ID_EX_p22), .b(ID_EX_p25), .c_i(1'b0), .s(RS1__plus__IMM_s));  // open: c_o
  Add #(.Bits(32)) PC__plus__IMM (.a(ID_EX_p26), .b(ID_EX_p25), .c_i(1'b0), .s(PC__plus__IMM_s));  // open: c_o
  Multiplexer #(.Selector_Bits(2), .Bits(32)) multiplexer_2 (
    .sel(ID_EX_p28), .in_0(ID_EX_p22), .in_1(bitextender_3_out), .in_2(MEM_WB_aresout), .in_3(WbBackup_q),
    .out(multiplexer_2_out));
  Multiplexer #(.Selector_Bits(3), .Bits(32)) multiplexer_3 (
    .sel(ID_EX_p29), .in_0(ID_EX_p23), .in_1(ID_EX_p25), .in_2(bitextender_3_out), .in_3(MEM_WB_aresout),
    .in_4(WbBackup_q), .in_5({32{1'b0}}), .in_6({32{1'b0}}), .in_7({32{1'b0}}), .out(multiplexer_3_out));
  ula ALU (.E1(multiplexer_2_out), .E2(multiplexer_3_out), .Controle(ID_EX_p19), .S({ALU_s_2, ALU_s}), .Zero(ALU_zero));
  ExM EX_MEM (
    .RwIn(ID_EX_p16), .MwIn(ID_EX_p17), .ResIn(ID_EX_p18), .MrIn(ID_EX_p21), .AresIn(ALU_s),
    .DbIn(ID_EX_p23), .RdIn(ID_EX_p24), .Pc_plus_4In(ID_EX_p27), .CLK(clk), .RwOut(EX_MEM_rwout),
    .MwOut(EX_MEM_mwout), .ResOut(EX_MEM_resout), .MrOut(EX_MEM_mrout), .AresOut(EX_MEM_aresout),
    .DbOut(EX_MEM_dbout), .RdOut(EX_MEM_rdout), .Pc_plus_4Out(EX_MEM_pc_plus_4out));
  BitExtender #(.inputBits(24), .outputBits(32)) bitextender_3 (.in(EX_MEM_aresout), .out(bitextender_3_out));
  RAMDualPort #(.AddrBits(24), .Bits(32)) \Memória_de_Dados  (
    .A(EX_MEM_aresout), .Din(EX_MEM_dbout), .str(EX_MEM_mwout), .C(clk), .ld(EX_MEM_mrout),
    .D(\Memória_de_Dados_d ));
  MWB MEM_WB (
    .RwIn(EX_MEM_rwout), .ResIn(EX_MEM_resout), .MemIn(\Memória_de_Dados_d ), .AresIn(bitextender_3_out),
    .RdIn(EX_MEM_rdout), .Pc_plus_4In(EX_MEM_pc_plus_4out), .CLK(clk), .RwOut(MEM_WB_rwout),
    .ResOut(MEM_WB_resout), .MemOut(MEM_WB_memout), .AresOut(MEM_WB_aresout), .RdOut(MEM_WB_rdout),
    .Pc_plus_4Out(MEM_WB_pc_plus_4out));
  Multiplexer #(.Selector_Bits(2), .Bits(32)) multiplexer_4 (
    .sel(MEM_WB_resout), .in_0(MEM_WB_aresout), .in_1(MEM_WB_memout), .in_2(MEM_WB_pc_plus_4out),
    .in_3({32{1'b0}}), .out(multiplexer_4_out));
  Register #(.Bits(32)) WbBackup (.D(multiplexer_4_out), .C(clk), .en(1'b1), .Q(WbBackup_q));

  // Notes on the sheet:
  //   clk: Hz: 10
  //   contents of Memória_de_Instruções (hex, n*v repeats v):
  //   fc10297,0,0,0,28293,0,0,0,1000313,0,0,0,630eb3,0,0,0,3200393,0,0,0
  //   ,ffb00e13,0,0,0,738f33,0,0,0,1d2a023,0,0,0,1d30663,0,0,0,1ce0fb3
  //   ,0,0,0,2a583
endmodule
