// Digital circuit SignExtender.dig as structural Verilog
module SignExtender (
  input  [1:0] ImmSrc,
  input  [24:0] OpCode_31_7,
  output [31:0] EXT
);

  wire [31:0] B___Type_out, I___Type_out, J___Type_out, S___Type_out;

  BitExtender #(.inputBits(12), .outputBits(32)) I___Type (.in(OpCode_31_7[24:13]), .out(I___Type_out));
  BitExtender #(.inputBits(12), .outputBits(32)) S___Type (
    .in({OpCode_31_7[24:18], OpCode_31_7[4:0]}), .out(S___Type_out));
  BitExtender #(.inputBits(13), .outputBits(32)) B___Type (
    .in({OpCode_31_7[24], OpCode_31_7[0], OpCode_31_7[23:18], OpCode_31_7[4:1], 1'b0}), .out(B___Type_out));
  BitExtender #(.inputBits(20), .outputBits(32)) J___Type (
    .in({OpCode_31_7[12:5], OpCode_31_7[13], OpCode_31_7[23:14], 1'b0}), .out(J___Type_out));
  Multiplexer #(.Selector_Bits(2), .Bits(32)) multiplexer_1 (
    .sel(ImmSrc), .in_0(I___Type_out), .in_1(S___Type_out), .in_2(B___Type_out), .in_3(J___Type_out),
    .out(EXT));
endmodule
