// Digital circuit aluDecoder.dig as structural Verilog
module aluDecoder (
  input  [1:0] AluOp,
  input  [2:0] Funct3,
  input  Op_5,
  input  Funct7_5,
  output [2:0] ALUControl
);

  wire and_1_out, and_2_out, and_3_out, and_4_out, and_5_out, and_6_out, and_7_out, and_8_out, and_9_out,
       and_10_out, and_11_out, not_1_out, not_2_out, not_3_out, not_4_out, not_5_out;

  not not_1 (not_1_out, AluOp[1]);
  not not_2 (not_2_out, AluOp[0]);
  not not_3 (not_3_out, Funct3[2]);
  not not_4 (not_4_out, Funct3[1]);
  not not_5 (not_5_out, Funct3[0]);
  and and_1 (and_1_out, AluOp[1], not_2_out, not_3_out, not_4_out, Funct3[0]);
  and and_2 (and_2_out, AluOp[1], not_2_out, not_3_out, Funct3[1], not_5_out);
  and and_3 (and_3_out, AluOp[1], not_2_out, Funct3[2], not_4_out, not_5_out);
  and and_4 (and_4_out, not_1_out, AluOp[0], not_4_out);
  and and_5 (and_5_out, AluOp[1], not_2_out, Funct3[1], not_5_out);
  and and_6 (and_6_out, AluOp[1], not_2_out, Funct3[2], Funct3[1]);
  and and_7 (and_7_out, not_1_out, AluOp[0], not_4_out);
  and and_8 (and_8_out, AluOp[1], not_2_out, not_3_out, not_5_out, Op_5, Funct7_5);
  and and_9 (and_9_out, AluOp[1], not_2_out, not_3_out, not_4_out, Funct3[0]);
  and and_10 (and_10_out, AluOp[1], not_2_out, Funct3[1], not_5_out);
  and and_11 (and_11_out, not_1_out, AluOp[0], Funct3[2], not_4_out);
  or or_1 (ALUControl[1], and_5_out, and_6_out, and_7_out);
  or or_2 (ALUControl[2], and_1_out, and_2_out, and_3_out, and_4_out);
  or or_3 (ALUControl[0], and_8_out, and_9_out, and_10_out, and_11_out);
endmodule
