// Digital circuit mainDecoderV2.dig as structural Verilog
module mainDecoderV2 (
  input  [6:0] OpCode,
  output RegWrite,
  output [1:0] ImmSrc,
  output MemWrite,
  output [1:0] ResultSrc,
  output Branch,
  output [1:0] ALUOp,
  output [1:0] PCUpdate,
  output ALUSrc,
  output MemRead
);

  wire and_1_out, and_2_out, and_3_out, and_4_out, and_5_out, and_6_out, and_7_out, and_11_out, and_12_out,
       not_1_out, not_2_out, not_3_out, not_4_out, not_5_out, not_6_out, not_7_out, not_8_out, not_9_out,
       not_10_out, not_11_out, not_12_out, not_13_out, not_14_out, not_15_out, not_16_out, not_17_out,
       not_18_out, not_19_out, not_20_out, not_21_out, not_22_out, not_23_out, not_24_out, not_25_out,
       not_26_out, not_27_out, not_28_out, not_29_out, not_30_out, not_31_out, not_32_out, not_33_out,
       not_34_out, not_35_out, not_36_out;

  not not_1 (not_1_out, OpCode[6]);
  not not_2 (not_2_out, OpCode[6]);
  not not_3 (not_3_out, OpCode[5]);
  not not_4 (not_4_out, OpCode[4]);
  not not_5 (not_5_out, OpCode[3]);
  not not_6 (not_6_out, OpCode[4]);
  not not_7 (not_7_out, OpCode[3]);
  not not_8 (not_8_out, OpCode[4]);
  not not_9 (not_9_out, OpCode[3]);
  not not_10 (not_10_out, OpCode[4]);
  not not_11 (not_11_out, OpCode[3]);
  not not_12 (not_12_out, OpCode[2]);
  not not_13 (not_13_out, OpCode[2]);
  not not_14 (not_14_out, OpCode[2]);
  and and_1 (and_1_out, not_1_out, OpCode[4], not_5_out, not_12_out, OpCode[1], OpCode[0]);
  and and_2 (and_2_out, not_1_out, not_3_out, not_5_out, not_12_out, OpCode[1], OpCode[0]);
  and and_3 (and_3_out, OpCode[6], OpCode[5], not_4_out, OpCode[2], OpCode[1], OpCode[0]);
  and and_4 (and_4_out, OpCode[6], OpCode[5], not_6_out, not_7_out, not_13_out, OpCode[1], OpCode[0]);
  and and_5 (and_5_out, OpCode[6], OpCode[5], not_6_out, OpCode[3], OpCode[2], OpCode[1], OpCode[0]);
  and and_6 (and_6_out, OpCode[6], OpCode[5], not_6_out, OpCode[3], OpCode[2], OpCode[1], OpCode[0]);
  and and_7 (and_7_out, not_2_out, OpCode[5], not_7_out, not_13_out, OpCode[1], OpCode[0]);
  and and_8 (Branch, OpCode[6], OpCode[5], not_8_out, not_9_out, not_14_out, OpCode[1], OpCode[0]);
  and and_9 (PCUpdate[1], OpCode[6], OpCode[5], not_10_out, not_11_out, OpCode[2], OpCode[1], OpCode[0]);
  and and_10 (PCUpdate[0], OpCode[6], OpCode[5], not_10_out, OpCode[3], OpCode[2], OpCode[1], OpCode[0]);
  or or_1 (RegWrite, and_1_out, and_2_out, and_3_out);
  or or_2 (ImmSrc[1], and_4_out, and_5_out);
  or or_3 (ImmSrc[0], and_6_out, and_7_out);
  not not_15 (not_15_out, OpCode[6]);
  not not_16 (not_16_out, OpCode[6]);
  not not_17 (not_17_out, OpCode[5]);
  not not_18 (not_18_out, OpCode[6]);
  not not_19 (not_19_out, OpCode[5]);
  not not_20 (not_20_out, OpCode[6]);
  not not_21 (not_21_out, OpCode[4]);
  not not_22 (not_22_out, OpCode[4]);
  not not_23 (not_23_out, OpCode[3]);
  not not_24 (not_24_out, OpCode[4]);
  not not_25 (not_25_out, OpCode[3]);
  not not_26 (not_26_out, OpCode[4]);
  not not_27 (not_27_out, OpCode[5]);
  not not_28 (not_28_out, OpCode[3]);
  not not_29 (not_29_out, OpCode[2]);
  not not_30 (not_30_out, OpCode[2]);
  not not_31 (not_31_out, OpCode[2]);
  not not_32 (not_32_out, OpCode[3]);
  not not_33 (not_33_out, OpCode[2]);
  not not_34 (not_34_out, OpCode[4]);
  not not_35 (not_35_out, OpCode[3]);
  not not_36 (not_36_out, OpCode[2]);
  and and_11 (and_11_out, not_15_out, not_21_out, not_28_out, not_29_out, OpCode[1], OpCode[0]);
  and and_12 (and_12_out, not_15_out, not_19_out, not_28_out, not_29_out, OpCode[1], OpCode[0]);
  and and_13 (MemWrite, not_16_out, OpCode[5], not_22_out, not_23_out, not_30_out, OpCode[1], OpCode[0]);
  and and_14 (ResultSrc[1], OpCode[5], OpCode[5], not_24_out, OpCode[2], OpCode[1], OpCode[0]);
  and and_15 (ResultSrc[0], not_17_out, not_24_out, not_25_out, not_31_out, OpCode[1], OpCode[0]);
  and and_16 (ALUOp[1], not_18_out, OpCode[4], not_32_out, not_33_out, OpCode[1], OpCode[0]);
  and and_17 (ALUOp[0], OpCode[6], OpCode[5], not_26_out, not_32_out, OpCode[1], OpCode[0]);
  and and_18 (MemRead, not_20_out, not_27_out, not_34_out, not_35_out, not_36_out, OpCode[1], OpCode[0]);
  or or_4 (ALUSrc, and_11_out, and_12_out);
endmodule
