// Digital circuit ula.dig as structural Verilog
module ula (
  input  [31:0] E1,
  input  [31:0] E2,
  input  [2:0] Controle,
  output [31:0] S,
  output Zero
);

  wire SLT_eq, SLT_lt;
  wire [31:0] add_1_s, and_1_out, bitextender_1_out, bitextender_2_out, not_1_out, or_1_out, SLL_out,
       sub_1_s, xor_1_out;

  Add #(.Bits(32)) add_1 (.a(E1), .b(E2), .c_i(1'b0), .s(add_1_s));  // open: c_o
  Sub #(.Bits(32)) sub_1 (.a(E1), .b(E2), .c_i(1'b0), .s(sub_1_s));  // open: c_o
  assign and_1_out = E1 & E2;  // And and_1, 32 bits wide
  assign or_1_out = E1 | E2;  // Or or_1, 32 bits wide
  assign xor_1_out = E1 ^ E2;  // XOr xor_1, 32 bits wide
  BarrelShifter #(.Bits(32)) SLL (.in(E1), .shift(E2[5:0]), .out(SLL_out));
  Comparator #(.Bits(32)) SLT (.a(E1), .b(E2), .eq(SLT_eq), .lt(SLT_lt));  // open: gt
  BitExtender #(.inputBits(1), .outputBits(32)) bitextender_1 (.in(SLT_eq), .out(bitextender_1_out));
  BitExtender #(.inputBits(1), .outputBits(32)) bitextender_2 (.in(SLT_lt), .out(bitextender_2_out));
  assign not_1_out = ~bitextender_1_out;  // Not not_1, 32 bits wide
  Multiplexer #(.Selector_Bits(3), .Bits(32)) multiplexer_1 (
    .sel(Controle), .in_0(add_1_s), .in_1(sub_1_s), .in_2(and_1_out), .in_3(or_1_out), .in_4(xor_1_out),
    .in_5(SLL_out), .in_6(not_1_out), .in_7(bitextender_2_out), .out(S));
  Comparator #(.Bits(32)) comparator_1 (.a(S), .b({32{1'b0}}), .eq(Zero));  // open: gt, lt
endmodule
